# Fritzing sketch avionics (saved by Fritzing 0.8.7b)

parts:
  Arduino_Nano = Arduino Nano (Rev3.0)
  SRV_ELEV = Basic Servo
  SRV_AIL_L = Basic Servo
  SRV_AIL_R = Basic Servo
  SRV_RUDD = Basic Servo
  ESC_1 = mystery part, 3 pins [chip_label=ESC]
  WIFI = mystery part, 8 pins [chip_label=NRF24L01+]
  VCC1 = 4 x AAA Battery Mount

nets:
  N1: Arduino_Nano.D3, ESC_1.pin1
  N2: Arduino_Nano.D5, SRV_ELEV.pulse
  N3: Arduino_Nano.D6, SRV_RUDD.pulse
  N4: Arduino_Nano.D7, WIFI.pin2
  N5: Arduino_Nano.D8, WIFI.pin7
  N6: Arduino_Nano.D9, SRV_AIL_R.pulse
  N7: Arduino_Nano.D10, SRV_AIL_L.pulse
  N8: Arduino_Nano.D11/MOSI, WIFI.pin6
  N9: Arduino_Nano.D12/MISO, WIFI.pin4
  VCC: Arduino_Nano.VIN, SRV_ELEV.vcc, SRV_AIL_L.vcc, SRV_AIL_R.vcc, SRV_RUDD.vcc, ESC_1.pin2, VCC1.+
  GND: Arduino_Nano.GND, SRV_ELEV.gnd, SRV_AIL_L.gnd, SRV_AIL_R.gnd, SRV_RUDD.gnd, WIFI.pin1
  N10: Arduino_Nano.3V3, WIFI.pin8
  N11: Arduino_Nano.D13/SCK, WIFI.pin3
  N12: ESC_1.pin3, VCC1.-

notes:
  SPI_bus
